# Fritzing sketch alimentador (saved by Fritzing 0.9.3b)
breadboards: 1

parts:
  Componente1 = Arduino Uno (Rev3)
  Raspberry_Pi_1 = Raspberry Pi 3 [part_number=RPI-3-V1.2]  # not connected
  T1 = TMP36 Temperature Sensor [package="TO92 [THT]"]
  J1 = Basic Servo
  U1 = 2-Channel 5v Relay Shield [package=relay-2ch5v10a]
  Componente3 = HX711 Weighing Sensor Module
  Load_Cell1 = Load Cell - Red/white/black/green
  J2 = Piezo Speaker

nets:
  N1: Componente1.A0, Componente3.DO/RX
  N2: Componente1.A1, Componente3.CK/TX
  N3: Componente1.A2, T1.Vout
  N4: Componente1.D8, U1.IN1
  N5: Componente1.D2, J1.pulse
  N6: Componente1.D3_PWM, J2.pin2
  VCC: Componente1.5V, T1.+Vs, U1.VCC, Componente3.VCC
  GND: Componente1.GND, T1.GND, U1.GND, Componente3.GND
  N7: Componente3.E+, Load_Cell1.wire1
  N8: Componente3.E-, Load_Cell1.wire3
  N9: Componente3.A+, Load_Cell1.wire2
  N10: Componente3.A-, Load_Cell1.wire4

custom parts:
  2-Channel 5v Relay Shield: 2 Channel 5v Relay Shield w. 2x SPD-06VDC-SD-C
  Load Cell - Red/white/black/green: A rectangle load cell/weighting pressure Sensor with four wires - Red, white, black, green. Normally corresponding with E+, E-, A+, A- respectively.
