# Fritzing sketch wemos esp32s (saved by Fritzing 0.9.3b)

parts:
  RHT1 = Humidity and Temperature Sensor RHT03
  Componente1 = Tri-Axis Gyro Breakout - L3G4200D
  LED1 = RGB LED (com. cathode, rbg) [package="5 mm [THT]"]
  R1 = PHOTOCELL [package=photocell-kit]
  R2 = Resistor [tolerance=±5% resistance=330 package="2010 [SMD]"]
  R3 = Resistor [tolerance=±5% resistance=330 package="2010 [SMD]"]
  R4 = Resistor [tolerance=±5% resistance=330 package="2010 [SMD]"]
  R5 = Resistor [tolerance=±5% resistance=10k package="2010 [SMD]"]
  R6 = Resistor [tolerance=±5% resistance=4.7k package="2010 [SMD]"]  # not connected
  DS1 = DS18B20 1-Wire Temperature Sensor [part_number=DS18B20]
  U2 = ESP32S WEMOS PELO AMOR DE DEUS V77 [part_number=WEMOS]

nets:
  VCC: RHT1.Vcc, Componente1.VCC, LED1.common_cathode, R5.Pin_0, DS1.VDD, U2.VIN
  N1: RHT1.Data-signal, U2.GPIO27
  GND: RHT1.GND_2, Componente1.GND, R1.P$1, DS1.GND, U2.GND, U2.GPIO4
  N2: Componente1.SCL, U2.GPIO18
  N3: Componente1.SDA, U2.GPIO19
  N4: R1.P$2, R5.Pin_1, U2.GPIO32
  N5: R2.Pin_0, U2.GPIO33
  N6: R3.Pin_0, U2.GPIO35
  N7: R4.Pin_0, U2.GPIO34
  N8: DS1.DQ, U2.GPIO25

custom parts:
  ESP32S WEMOS PELO AMOR DE DEUS V77: WEMS ESP32S
